# Fritzing sketch RFID_Raspberry_Pi_4 (saved by Fritzing 0.9.7b)
breadboards: 1

parts:
  Componente2 = RFID-RC522-v2
  Mod1 = Raspberry Pi 4B

nets:
  N1: Componente2.SDA, Mod1.GPIO8
  N2: Componente2.SCK, Mod1.GPIO11
  N3: Componente2.MOSI, Mod1.GPIO10
  N4: Componente2.MISO, Mod1.GPIO9
  N5: Componente2.RST, Mod1.GPIO25
  N6: Componente2.3_3V, Mod1.3V3

custom parts:
  RFID-RC522-v2: A simple China made RFID-RC522 Reader; do check the pin labels, as this is a MFRC522 based clone.
